// Logisim project lab03.circ as structural Verilog
module \дешифратор  (
  input  [3:0] in_1
);

  wire and_1_out, and_2_out, and_3_out, and_4_out, and_5_out, and_6_out, and_7_out, and_8_out, and_9_out,
       and_10_out, and_11_out, and_12_out, and_13_out, and_14_out, and_15_out, and_16_out, and_17_out,
       and_18_out, and_19_out, and_20_out, and_21_out, and_22_out, and_23_out, and_24_out, and_25_out,
       and_26_out, and_27_out, and_28_out, and_29_out, and_30_out, not_1_out, not_2_out, not_3_out,
       not_4_out, not_5_out, not_6_out, not_7_out, not_8_out, not_9_out, not_10_out, not_11_out, not_12_out,
       not_13_out, not_14_out, not_15_out, not_16_out, not_17_out, not_18_out, not_19_out, not_20_out,
       not_21_out, not_22_out, not_23_out, not_24_out, not_25_out, not_26_out, not_27_out, not_28_out,
       not_29_out, not_30_out, not_31_out, not_32_out, not_33_out, not_34_out, not_35_out, not_36_out,
       not_37_out, or_1_out, or_2_out, or_3_out, or_4_out, or_5_out, or_6_out, or_7_out, or_8_out;

  // Probe on in_1
  not not_1 (not_1_out, in_1[2]);
  not not_2 (not_2_out, in_1[0]);
  not not_3 (not_3_out, in_1[3]);
  not not_4 (not_4_out, in_1[1]);
  not not_5 (not_5_out, in_1[2]);
  not not_6 (not_6_out, in_1[1]);
  not not_7 (not_7_out, in_1[0]);
  not not_8 (not_8_out, in_1[1]);
  not not_9 (not_9_out, in_1[0]);
  not not_10 (not_10_out, in_1[2]);
  not not_11 (not_11_out, in_1[0]);
  not not_12 (not_12_out, in_1[3]);
  not not_13 (not_13_out, in_1[1]);
  not not_14 (not_14_out, in_1[0]);
  not not_15 (not_15_out, in_1[3]);
  not not_16 (not_16_out, in_1[1]);
  not not_17 (not_17_out, in_1[3]);
  not not_18 (not_18_out, in_1[0]);
  not not_19 (not_19_out, in_1[2]);
  not not_20 (not_20_out, in_1[1]);
  not not_21 (not_21_out, in_1[3]);
  not not_22 (not_22_out, in_1[1]);
  not not_23 (not_23_out, in_1[3]);
  not not_24 (not_24_out, in_1[1]);
  not not_25 (not_25_out, in_1[3]);
  not not_26 (not_26_out, in_1[2]);
  not not_27 (not_27_out, in_1[3]);
  not not_28 (not_28_out, in_1[2]);
  not not_29 (not_29_out, in_1[0]);
  not not_30 (not_30_out, in_1[2]);
  not not_31 (not_31_out, in_1[1]);
  not not_32 (not_32_out, in_1[0]);
  not not_33 (not_33_out, in_1[1]);
  not not_34 (not_34_out, in_1[2]);
  not not_35 (not_35_out, in_1[0]);
  not not_36 (not_36_out, in_1[0]);
  and and_1 (and_1_out, not_1_out, in_1[1]);
  and and_2 (and_2_out, in_1[1], not_2_out);
  and and_3 (and_3_out, not_3_out, in_1[2], not_4_out);
  and and_4 (and_4_out, in_1[3], not_5_out);
  and and_5 (and_5_out, in_1[3], in_1[1]);
  and and_6 (and_6_out, not_6_out, not_7_out);
  and and_7 (and_7_out, in_1[2], not_8_out);
  and and_8 (and_8_out, in_1[2], not_9_out);
  and and_9 (and_9_out, not_10_out, not_11_out);
  and and_10 (and_10_out, in_1[2], in_1[0]);
  and and_11 (and_11_out, not_12_out, not_13_out, not_14_out);
  not not_37 (not_37_out, in_1[2]);
  and and_12 (and_12_out, not_15_out, in_1[1], in_1[0]);
  and and_13 (and_13_out, in_1[3], not_16_out, in_1[0]);
  and and_14 (and_14_out, not_17_out, in_1[2], in_1[1], not_18_out);
  and and_15 (and_15_out, in_1[3], not_19_out, in_1[1], in_1[0]);
  and and_16 (and_16_out, in_1[3], in_1[2], not_20_out, in_1[0]);
  and and_17 (and_17_out, not_21_out, not_22_out);
  and and_18 (and_18_out, not_23_out, in_1[0]);
  and and_19 (and_19_out, not_24_out, in_1[0]);
  and and_20 (and_20_out, not_25_out, in_1[2]);
  and and_21 (and_21_out, in_1[3], not_26_out);
  and and_22 (and_22_out, not_27_out, not_28_out, not_29_out);
  and and_23 (and_23_out, not_30_out, in_1[1], in_1[0]);
  and and_24 (and_24_out, in_1[2], not_31_out, in_1[0]);
  and and_25 (and_25_out, in_1[2], in_1[1], not_32_out);
  and and_26 (and_26_out, in_1[3], not_33_out);
  and and_27 (and_27_out, not_34_out, not_35_out);
  and and_28 (and_28_out, in_1[1], not_36_out);
  and and_29 (and_29_out, in_1[3], in_1[1]);
  and and_30 (and_30_out, in_1[3], in_1[2]);
  or or_1 (or_1_out, and_1_out, and_2_out, and_3_out, and_4_out, and_5_out);
  or or_2 (or_2_out, and_6_out, and_7_out, and_8_out, in_1[3]);
  or or_3 (or_3_out, and_9_out, in_1[1], and_10_out, in_1[3]);
  or or_4 (or_4_out, and_11_out, not_37_out, and_12_out, and_13_out);
  or or_5 (or_5_out, and_14_out, and_15_out, and_16_out);
  or or_6 (or_6_out, and_17_out, and_18_out, and_19_out, and_20_out, and_21_out);
  or or_7 (or_7_out, and_22_out, and_23_out, and_24_out, and_25_out, and_26_out);
  or or_8 (or_8_out, and_27_out, and_28_out, and_29_out, and_30_out);
  _7_Segment_Display u_7_segment_display_1 (
    .g(or_1_out), .f(or_2_out), .a(or_3_out), .b(or_4_out), .e(or_8_out), .d(or_7_out), .c(or_6_out),
    .dp(or_5_out));
endmodule

module \шифратор_с_проверкой  (
  input  _0,
  input  _1,
  input  _2,
  input  _3,
  input  _4,
  input  _5,
  input  _6,
  input  _7,
  input  _8,
  input  _9,
  input  _10,
  input  _11,
  input  _12,
  input  _13,
  input  _14,
  input  _15,
  output [3:0] out_17,
  output \Неправильный_ввод 
);

  wire or_1_out, or_2_out, or_3_out, or_4_out;

  or or_1 (or_1_out, _1, _3, _5, _7, _9, _11, _13, _15);
  or or_2 (or_2_out, _2, _3, _6, _7, _10, _11, _14, _15);
  or or_3 (or_3_out, _4, _5, _6, _7, _12, _13, _14, _15);
  or or_4 (or_4_out, _8, _9, _10, _11, _12, _13, _14, _15);
  NotExactlyOne xnor_1 (
    .out(\Неправильный_ввод ), .in0(_15), .in1(_14), .in2(_13), .in3(_12), .in4(_11), .in5(_10), .in6(_9),
    .in7(_8), .in8(_7), .in9(_6), .in10(_5), .in11(_4), .in12(_3), .in13(_2), .in14(_1), .in15(_0));
  ExactlyOne xor_1 (.out(out_17[0]), .in0(or_1_out), .in1(\Неправильный_ввод ), .in2(\Неправильный_ввод ));
  ExactlyOne xor_2 (.out(out_17[1]), .in0(or_2_out), .in1(\Неправильный_ввод ), .in2(\Неправильный_ввод ));
  ExactlyOne xor_3 (.out(out_17[2]), .in0(or_3_out), .in1(\Неправильный_ввод ), .in2(\Неправильный_ввод ));
  ExactlyOne xor_4 (.out(out_17[3]), .in0(or_4_out), .in1(\Неправильный_ввод ), .in2(\Неправильный_ввод ));
  // Probe on out_17
endmodule

module \мультиплексор  (
  input  _0,
  input  _1,
  input  _2,
  input  _3,
  input  _4,
  input  _5,
  input  _6,
  input  _7,
  input  [2:0] in_9,
  output out_10
);

  wire and_1_out, and_2_out, and_3_out, and_4_out, and_5_out, and_6_out, and_7_out, and_8_out, not_1_out,
       not_2_out, not_3_out;

  // Probe on in_9
  not not_1 (not_1_out, in_9[2]);
  not not_2 (not_2_out, in_9[1]);
  not not_3 (not_3_out, in_9[0]);
  and and_1 (and_1_out, _0, not_1_out, not_2_out, not_3_out);
  and and_2 (and_2_out, _1, in_9[0], not_1_out, not_2_out);
  and and_3 (and_3_out, _2, in_9[1], not_1_out, not_3_out);
  and and_4 (and_4_out, _3, not_1_out, in_9[1], in_9[0]);
  and and_5 (and_5_out, _4, in_9[2], not_2_out, not_3_out);
  and and_6 (and_6_out, _5, in_9[2], in_9[0], not_2_out);
  and and_7 (and_7_out, _6, in_9[2], in_9[1], not_3_out);
  and and_8 (and_8_out, _7, in_9[2], in_9[1], in_9[0]);
  or or_1 (out_10, and_1_out, and_2_out, and_3_out, and_4_out, and_5_out, and_6_out, and_7_out, and_8_out);
endmodule

module \демультиплексор  (
  input  in_1,
  input  [2:0] in_2,
  output out_3,
  output out_4,
  output out_5,
  output out_6,
  output out_7,
  output out_8,
  output out_9,
  output out_10
);

  wire not_1_out, not_2_out, not_3_out;

  // Probe on in_2
  not not_1 (not_1_out, in_2[2]);
  not not_2 (not_2_out, in_2[0]);
  not not_3 (not_3_out, in_2[1]);
  and and_1 (out_3, in_1, not_3_out, not_2_out);
  and and_2 (out_4, in_1, in_2[0], not_3_out);
  and and_3 (out_5, in_1, in_2[1], not_1_out, not_2_out);
  and and_4 (out_6, in_1, not_1_out, in_2[1], in_2[0]);
  and and_5 (out_7, in_1, in_2[2], not_3_out, not_2_out);
  and and_6 (out_8, in_1, in_2[2], in_2[0], not_3_out);
  and and_7 (out_9, in_1, in_2[2], in_2[1], not_2_out);
  and and_8 (out_10, in_1, in_2[2], in_2[1], in_2[0]);
endmodule

module \шифратор  (
  input  _0,
  input  _1,
  input  _2,
  input  _3,
  input  _4,
  input  _5,
  input  _6,
  input  _7,
  input  _8,
  input  _9,
  input  _10,
  input  _11,
  input  _12,
  input  _13,
  input  _14,
  input  _15,
  output [3:0] out_17
);

  or or_1 (out_17[0], _1, _3, _5, _7, _9, _11, _13, _15);
  or or_2 (out_17[1], _2, _3, _6, _7, _10, _11, _14, _15);
  or or_3 (out_17[2], _4, _5, _6, _7, _12, _13, _14, _15);
  or or_4 (out_17[3], _8, _9, _10, _11, _12, _13, _14, _15);
  // Probe on out_17
endmodule
