// Logisim project laba3.circ as structural Verilog: 2 circuits, main circuit шифратор и дешифратор
module \шифратор_и_дешифратор  (
  input  _0,
  input  _1,
  input  _2,
  input  _3,
  input  _4,
  input  _5,
  input  _6,
  input  _7,
  input  _8,
  input  _9,
  input  _10,
  input  _11,
  input  _12,
  input  _13,
  input  _14,
  input  _15,
  output out_17,
  output out_18,
  output out_19,
  output out_20,
  output _0_2,
  output _1_2,
  output _2_2,
  output _3_2,
  output _4_2,
  output _5_2,
  output _6_2,
  output _7_2,
  output _8_2,
  output _9_2,
  output _10_2,
  output _11_2,
  output _12_2,
  output _13_2,
  output _14_2,
  output _15_2
);

  wire not_1_out, not_2_out, not_3_out, not_4_out, not_5_out, not_6_out, not_7_out, not_8_out, not_9_out,
       not_10_out, not_11_out, not_12_out, not_13_out, not_14_out, not_15_out, not_16_out, not_17_out,
       not_18_out, not_19_out, not_20_out, not_21_out, not_22_out, not_23_out, not_24_out, not_25_out,
       not_26_out, not_27_out, not_28_out;

  or or_1 (out_17, _15, _14, _13, _12, _11, _10, _9, _8);
  or or_2 (out_18, _15, _14, _13, _12, _7, _6, _5, _4);
  or or_3 (out_19, _15, _14, _11, _10, _7, _6, _3, _2);
  or or_4 (out_20, _15, _13, _11, _9, _7, _6, _3, _1);
  not not_1 (not_1_out, out_17);
  not not_2 (not_2_out, out_18);
  not not_3 (not_3_out, out_19);
  not not_4 (not_4_out, out_17);
  not not_5 (not_5_out, out_18);
  not not_6 (not_6_out, out_20);
  not not_7 (not_7_out, out_17);
  not not_8 (not_8_out, out_18);
  not not_9 (not_9_out, out_17);
  not not_10 (not_10_out, out_19);
  not not_11 (not_11_out, out_20);
  not not_12 (not_12_out, out_17);
  not not_13 (not_13_out, out_19);
  not not_14 (not_14_out, out_17);
  not not_15 (not_15_out, out_20);
  not not_16 (not_16_out, out_17);
  not not_17 (not_17_out, out_18);
  not not_18 (not_18_out, out_19);
  not not_19 (not_19_out, out_20);
  not not_20 (not_20_out, out_18);
  not not_21 (not_21_out, out_19);
  not not_22 (not_22_out, out_18);
  not not_23 (not_23_out, out_20);
  not not_24 (not_24_out, out_18);
  not not_25 (not_25_out, out_19);
  not not_26 (not_26_out, out_20);
  not not_27 (not_27_out, out_19);
  not not_28 (not_28_out, out_20);
  and and_1 (_1_2, not_1_out, not_2_out, not_3_out, out_20);
  and and_2 (_2_2, not_4_out, not_5_out, out_19, not_6_out);
  and and_3 (_3_2, not_7_out, not_8_out, out_19, out_20);
  and and_4 (_4_2, not_9_out, out_18, not_10_out, not_11_out);
  and and_5 (_5_2, not_12_out, out_18, not_13_out, out_20);
  and and_6 (_6_2, not_14_out, out_18, out_19, not_15_out);
  and and_7 (_7_2, not_16_out, out_18, out_19, out_20);
  and and_8 (_8_2, out_17, not_17_out, not_18_out, not_19_out);
  and and_9 (_9_2, out_17, not_20_out, not_21_out, out_20);
  and and_10 (_10_2, out_17, not_22_out, out_19, not_23_out);
  and and_11 (_11_2, out_17, not_24_out, out_19, out_20);
  and and_12 (_12_2, out_17, out_18, not_25_out, not_26_out);
  and and_13 (_13_2, out_17, out_18, not_27_out, out_20);
  and and_14 (_14_2, out_17, out_18, out_19, not_28_out);
  and and_15 (_15_2, out_17, out_18, out_19, out_20);

  assign _0_2 = _0;
endmodule

module \мультиплексор_и_демультиплексор  (
  input  in_1,
  input  in_2,
  input  in_3,
  input  in_4,
  input  in_5,
  input  in_6,
  output out_7,
  output out_8,
  output out_9,
  output out_10,
  output out_11,
  output out_12,
  output out_13,
  output out_14,
  output out_15
);

  wire and_1_out, and_2_out, and_3_out, and_4_out, not_1_out, not_2_out, not_3_out, not_4_out;

  and and_1 (and_1_out, in_1, out_12);
  and and_2 (and_2_out, in_2, out_13);
  and and_3 (and_3_out, in_3, out_14);
  and and_4 (and_4_out, in_4, out_15);
  not not_1 (not_1_out, in_5);
  and and_5 (out_12, not_1_out, not_2_out);
  not not_2 (not_2_out, in_6);
  not not_3 (not_3_out, in_5);
  and and_6 (out_13, not_3_out, in_6);
  and and_7 (out_14, in_5, not_4_out);
  not not_4 (not_4_out, in_6);
  and and_8 (out_15, in_5, in_6);
  or or_1 (out_8, and_1_out, and_2_out, and_3_out, and_4_out);
  and and_9 (out_7, out_8, out_12);
  and and_10 (out_9, out_8, out_13);
  and and_11 (out_10, out_8, out_14);
  and and_12 (out_11, out_8, out_15);
endmodule
